// Digital circuit alu.dig as structural Verilog
module alu (
  input  [7:0] N,
  input  [2:0] Opcode,
  input  clk,
  output [7:0] AC_out,
  output [7:0] MQ_out
);

  wire [7:0] divisor_1_ac_out, divisor_1_mq_out, multiplexer_1_out, multiplexer_2_out,
       multiplicador_1_ac_out, multiplicador_1_mq_out, nand8bits_1_s, shift_left_1_ac_out,
       shift_right_1_ac_out, somador8bits_1_s, subtrator8bits_1_s, xor8bits_1_s;

  somador8bits somador8bits_1 (.A(AC_out), .B(N), .Ci(1'b0), .S(somador8bits_1_s));  // open: Cout
  subtrator8bits subtrator8bits_1 (.A(AC_out), .B(N), .S(subtrator8bits_1_s));  // open: Cout
  multiplicador multiplicador_1 (.A(AC_out), .B(N), .AC_out(multiplicador_1_ac_out), .MQ_out(multiplicador_1_mq_out));
  divisor divisor_1 (.A(AC_out), .B(N), .AC_out(divisor_1_ac_out), .MQ_out(divisor_1_mq_out));
  nand8bits nand8bits_1 (.A(AC_out), .B(N), .S(nand8bits_1_s));
  xor8bits xor8bits_1 (.A(AC_out), .B(N), .S(xor8bits_1_s));
  shift_left shift_left_1 (.A(AC_out), .AC_out(shift_left_1_ac_out));
  shift_right shift_right_1 (.A(AC_out), .AC_out(shift_right_1_ac_out));
  Multiplexer #(.Bits(8), .Selector_Bits(3)) multiplexer_1 (
    .sel(Opcode), .in_0(somador8bits_1_s), .in_1(subtrator8bits_1_s), .in_2(multiplicador_1_ac_out),
    .in_3(divisor_1_ac_out), .in_4(nand8bits_1_s), .in_5(xor8bits_1_s), .in_6(shift_left_1_ac_out),
    .in_7(shift_right_1_ac_out), .out(multiplexer_1_out));
  Multiplexer #(.Bits(8), .Selector_Bits(3)) multiplexer_2 (
    .sel(Opcode), .in_0({8{1'b0}}), .in_1({8{1'b0}}), .in_2(multiplicador_1_mq_out), .in_3(divisor_1_mq_out),
    .in_4({8{1'b0}}), .in_5({8{1'b0}}), .in_6({8{1'b0}}), .in_7({8{1'b0}}), .out(multiplexer_2_out));
  Register #(.Bits(8)) AC (.D(multiplexer_1_out), .C(clk), .en(1'b1), .Q(AC_out));
  Register #(.Bits(8)) MQ (.D(multiplexer_2_out), .C(clk), .en(1'b1), .Q(MQ_out));
endmodule
