// Digital circuit divisor.dig as structural Verilog
module divisor (
  input  [7:0] A,
  input  [7:0] B,
  output [7:0] AC_out,
  output [7:0] MQ_out
);

  wire [7:0] multiplexer_1_out, multiplexer_2_out, multiplexer_3_out, multiplexer_4_out, multiplexer_5_out,
       multiplexer_6_out, multiplexer_7_out, subtrator8bits_1_s, subtrator8bits_2_s, subtrator8bits_3_s,
       subtrator8bits_4_s, subtrator8bits_5_s, subtrator8bits_6_s, subtrator8bits_7_s, subtrator8bits_8_s;

  subtrator8bits subtrator8bits_1 (.A({{7{1'b0}}, A[7]}), .B(B), .S(subtrator8bits_1_s), .Cout(MQ_out[7]));
  Multiplexer #(.Bits(8)) multiplexer_1 (
    .sel(MQ_out[7]), .in_0({{7{1'b0}}, A[7]}), .in_1(subtrator8bits_1_s), .out(multiplexer_1_out));
  subtrator8bits subtrator8bits_2 (.A({multiplexer_1_out[6:0], A[6]}), .B(B), .S(subtrator8bits_2_s), .Cout(MQ_out[6]));
  Multiplexer #(.Bits(8)) multiplexer_2 (
    .sel(MQ_out[6]), .in_0({multiplexer_1_out[6:0], A[6]}), .in_1(subtrator8bits_2_s), .out(multiplexer_2_out));
  subtrator8bits subtrator8bits_3 (.A({multiplexer_2_out[6:0], A[5]}), .B(B), .S(subtrator8bits_3_s), .Cout(MQ_out[5]));
  Multiplexer #(.Bits(8)) multiplexer_3 (
    .sel(MQ_out[5]), .in_0({multiplexer_2_out[6:0], A[5]}), .in_1(subtrator8bits_3_s), .out(multiplexer_3_out));
  subtrator8bits subtrator8bits_4 (.A({multiplexer_3_out[6:0], A[4]}), .B(B), .S(subtrator8bits_4_s), .Cout(MQ_out[4]));
  Multiplexer #(.Bits(8)) multiplexer_4 (
    .sel(MQ_out[4]), .in_0({multiplexer_3_out[6:0], A[4]}), .in_1(subtrator8bits_4_s), .out(multiplexer_4_out));
  subtrator8bits subtrator8bits_5 (.A({multiplexer_4_out[6:0], A[3]}), .B(B), .S(subtrator8bits_5_s), .Cout(MQ_out[3]));
  Multiplexer #(.Bits(8)) multiplexer_5 (
    .sel(MQ_out[3]), .in_0({multiplexer_4_out[6:0], A[3]}), .in_1(subtrator8bits_5_s), .out(multiplexer_5_out));
  subtrator8bits subtrator8bits_6 (.A({multiplexer_5_out[6:0], A[2]}), .B(B), .S(subtrator8bits_6_s), .Cout(MQ_out[2]));
  Multiplexer #(.Bits(8)) multiplexer_6 (
    .sel(MQ_out[2]), .in_0({multiplexer_5_out[6:0], A[2]}), .in_1(subtrator8bits_6_s), .out(multiplexer_6_out));
  subtrator8bits subtrator8bits_7 (.A({multiplexer_6_out[6:0], A[1]}), .B(B), .S(subtrator8bits_7_s), .Cout(MQ_out[1]));
  Multiplexer #(.Bits(8)) multiplexer_7 (
    .sel(MQ_out[1]), .in_0({multiplexer_6_out[6:0], A[1]}), .in_1(subtrator8bits_7_s), .out(multiplexer_7_out));
  subtrator8bits subtrator8bits_8 (.A({multiplexer_7_out[6:0], A[0]}), .B(B), .S(subtrator8bits_8_s), .Cout(MQ_out[0]));
  Multiplexer #(.Bits(8)) multiplexer_8 (
    .sel(MQ_out[0]), .in_0({multiplexer_7_out[6:0], A[0]}), .in_1(subtrator8bits_8_s), .out(AC_out));
endmodule
