// Digital circuit fullAdder.dig as structural Verilog
module fullAdder (
  input  A,
  input  B,
  input  Ci,
  output S,
  output Co
);

  wire halfadder_1_co, halfadder_1_s, halfadder_2_co;

  halfAdder halfadder_1 (.A(A), .B(B), .S(halfadder_1_s), .Co(halfadder_1_co));
  halfAdder halfadder_2 (.A(halfadder_1_s), .B(Ci), .S(S), .Co(halfadder_2_co));
  or or_1 (Co, halfadder_2_co, halfadder_1_co);
endmodule
