// Digital circuit multiplicador.dig as structural Verilog
module multiplicador (
  input  [7:0] A,
  input  [7:0] B,
  output [7:0] AC_out,
  output [7:0] MQ_out
);

  wire [7:0] multiplexer_1_out, multiplexer_2_out, multiplexer_3_out, multiplexer_4_out, multiplexer_5_out,
       multiplexer_6_out, multiplexer_7_out, multiplexer_8_out;
  wire [15:0] somador16bits_1_s, somador16bits_2_s, somador16bits_3_s, somador16bits_4_s, somador16bits_5_s,
       somador16bits_6_s;

  Multiplexer #(.Bits(8)) multiplexer_1 (.sel(B[0]), .in_0({8{1'b0}}), .in_1(A), .out(multiplexer_1_out));
  Multiplexer #(.Bits(8)) multiplexer_2 (.sel(B[1]), .in_0({8{1'b0}}), .in_1(A), .out(multiplexer_2_out));
  Multiplexer #(.Bits(8)) multiplexer_3 (.sel(B[2]), .in_0({8{1'b0}}), .in_1(A), .out(multiplexer_3_out));
  Multiplexer #(.Bits(8)) multiplexer_4 (.sel(B[3]), .in_0({8{1'b0}}), .in_1(A), .out(multiplexer_4_out));
  Multiplexer #(.Bits(8)) multiplexer_5 (.sel(B[4]), .in_0({8{1'b0}}), .in_1(A), .out(multiplexer_5_out));
  Multiplexer #(.Bits(8)) multiplexer_6 (.sel(B[5]), .in_0({8{1'b0}}), .in_1(A), .out(multiplexer_6_out));
  Multiplexer #(.Bits(8)) multiplexer_7 (.sel(B[6]), .in_0({8{1'b0}}), .in_1(A), .out(multiplexer_7_out));
  Multiplexer #(.Bits(8)) multiplexer_8 (.sel(B[7]), .in_0({8{1'b0}}), .in_1(A), .out(multiplexer_8_out));
  somador16bits somador16bits_1 (
    .A({{8{1'b0}}, multiplexer_1_out}), .B({{7{1'b0}}, multiplexer_2_out, 1'b0}), .S(somador16bits_1_s));  // open: Cout
  somador16bits somador16bits_2 (
    .A(somador16bits_1_s), .B({{6{1'b0}}, multiplexer_3_out, 2'b00}), .S(somador16bits_2_s));  // open: Cout
  somador16bits somador16bits_3 (
    .A(somador16bits_2_s), .B({{5{1'b0}}, multiplexer_4_out, 3'b000}), .S(somador16bits_3_s));  // open: Cout
  somador16bits somador16bits_4 (
    .A(somador16bits_3_s), .B({4'b0000, multiplexer_5_out, 4'b0000}), .S(somador16bits_4_s));  // open: Cout
  somador16bits somador16bits_5 (
    .A(somador16bits_4_s), .B({3'b000, multiplexer_6_out, {5{1'b0}}}), .S(somador16bits_5_s));  // open: Cout
  somador16bits somador16bits_6 (
    .A(somador16bits_5_s), .B({2'b00, multiplexer_7_out, {6{1'b0}}}), .S(somador16bits_6_s));  // open: Cout
  somador16bits somador16bits_7 (
    .A(somador16bits_6_s), .B({1'b0, multiplexer_8_out, {7{1'b0}}}), .S({MQ_out, AC_out}));  // open: Cout
endmodule
