// Digital circuit somador16bits.dig as structural Verilog
module somador16bits (
  input  [15:0] A,
  input  [15:0] B,
  output Cout,
  output [15:0] S
);

  wire somador8bits_1_cout;

  somador8bits somador8bits_1 (.A(A[7:0]), .B(B[7:0]), .Ci(1'b0), .S(S[7:0]), .Cout(somador8bits_1_cout));
  somador8bits somador8bits_2 (.A(A[15:8]), .B(B[15:8]), .Ci(somador8bits_1_cout), .S(S[15:8]), .Cout(Cout));
endmodule
