// Digital circuit somador8bits.dig as structural Verilog
module somador8bits (
  input  [7:0] A,
  input  [7:0] B,
  input  Ci,
  output [7:0] S,
  output Cout
);

  wire fulladder_1_co, fulladder_2_co, fulladder_3_co, fulladder_4_co, fulladder_5_co, fulladder_6_co,
       fulladder_7_co;

  fullAdder fulladder_1 (.A(A[0]), .B(B[0]), .Ci(Ci), .S(S[0]), .Co(fulladder_1_co));
  fullAdder fulladder_2 (.A(A[1]), .B(B[1]), .Ci(fulladder_1_co), .S(S[1]), .Co(fulladder_2_co));
  fullAdder fulladder_3 (.A(A[2]), .B(B[2]), .Ci(fulladder_2_co), .S(S[2]), .Co(fulladder_3_co));
  fullAdder fulladder_4 (.A(A[3]), .B(B[3]), .Ci(fulladder_3_co), .S(S[3]), .Co(fulladder_4_co));
  fullAdder fulladder_5 (.A(A[4]), .B(B[4]), .Ci(fulladder_4_co), .S(S[4]), .Co(fulladder_5_co));
  fullAdder fulladder_6 (.A(A[5]), .B(B[5]), .Ci(fulladder_5_co), .S(S[5]), .Co(fulladder_6_co));
  fullAdder fulladder_7 (.A(A[6]), .B(B[6]), .Ci(fulladder_6_co), .S(S[6]), .Co(fulladder_7_co));
  fullAdder fulladder_8 (.A(A[7]), .B(B[7]), .Ci(fulladder_7_co), .S(S[7]), .Co(Cout));
endmodule
