// Digital circuit subtrator8bits.dig as structural Verilog
module subtrator8bits (
  input  [7:0] A,
  input  [7:0] B,
  output [7:0] S,
  output Cout
);

  wire fulladder_1_co, fulladder_2_co, fulladder_3_co, fulladder_4_co, fulladder_5_co, fulladder_6_co,
       fulladder_7_co;
  wire [7:0] not_1_out;

  assign not_1_out = ~B;  // Not not_1, 8 bits wide
  fullAdder fulladder_1 (.A(A[0]), .B(not_1_out[0]), .Ci(1'b1), .S(S[0]), .Co(fulladder_1_co));
  fullAdder fulladder_2 (.A(A[1]), .B(not_1_out[1]), .Ci(fulladder_1_co), .S(S[1]), .Co(fulladder_2_co));
  fullAdder fulladder_3 (.A(A[2]), .B(not_1_out[2]), .Ci(fulladder_2_co), .S(S[2]), .Co(fulladder_3_co));
  fullAdder fulladder_4 (.A(A[3]), .B(not_1_out[3]), .Ci(fulladder_3_co), .S(S[3]), .Co(fulladder_4_co));
  fullAdder fulladder_5 (.A(A[4]), .B(not_1_out[4]), .Ci(fulladder_4_co), .S(S[4]), .Co(fulladder_5_co));
  fullAdder fulladder_6 (.A(A[5]), .B(not_1_out[5]), .Ci(fulladder_5_co), .S(S[5]), .Co(fulladder_6_co));
  fullAdder fulladder_7 (.A(A[6]), .B(not_1_out[6]), .Ci(fulladder_6_co), .S(S[6]), .Co(fulladder_7_co));
  fullAdder fulladder_8 (.A(A[7]), .B(not_1_out[7]), .Ci(fulladder_7_co), .S(S[7]), .Co(Cout));
endmodule
